# Fritzing sketch bone-6502 (saved by Fritzing 0.7.4b)
breadboards: 2

parts:
  BeagleBone1 = beaglebone-a5
  IC1 = IC, DIP package, 40 pins [chip_label=WDC65C02S spacing=600mil]
  IC2 = IC, DIP package, 20 pins [chip_label="74HC245 - DOUT" spacing=300mil]
  IC3 = IC, DIP package, 20 pins [chip_label="74HC245 - ALO" spacing=300mil]
  IC4 = IC, DIP package, 20 pins [chip_label="74HC245 - AHI" spacing=300mil]
  IC5 = IC, DIP package, 20 pins [chip_label="74HC245 - DIN" spacing=300mil]
  R1 = Resistor [tolerance=±5% resistance=1k package=THT]
  R2 = Resistor [tolerance=±5% resistance=1k package=THT]
  R3 = Resistor [tolerance=±5% resistance=1k package=THT]
  R4 = Resistor [tolerance=±5% resistance=1k package=THT]
  R5 = Resistor [tolerance=±5% resistance=1k package=THT]
  R6 = Resistor [tolerance=±5% resistance=1k package=THT]
  R7 = Resistor [tolerance=±5% resistance=1k package=THT]
  R8 = Resistor [tolerance=±5% resistance=1k package=THT]

nets:
  N1: BeagleBone1.connectorp8-11, IC2.pin9
  N2: BeagleBone1.connectorp8-12, IC2.pin8
  N3: BeagleBone1.connectorp8-15, BeagleBone1.connectorp8-19, IC1.pin37
  N4: BeagleBone1.connectorp8-17, IC1.pin40, R5.Pin_1
  N5: BeagleBone1.connectorp8-18, IC1.pin34
  N6: BeagleBone1.connectorp8-20, IC2.pin7
  N7: BeagleBone1.connectorp8-21, IC2.pin6
  N8: BeagleBone1.connectorp8-27, IC2.pin2
  N9: BeagleBone1.connectorp8-28, IC2.pin4
  N10: BeagleBone1.connectorp8-29, IC2.pin3
  N11: BeagleBone1.connectorp8-30, IC2.pin5
  N12: BeagleBone1.connectorp8-39, IC3.pin12, IC4.pin12, IC5.pin12
  N13: BeagleBone1.connectorp8-40, IC3.pin11, IC4.pin11, IC5.pin11
  N14: BeagleBone1.connectorp8-41, IC3.pin14, IC4.pin14, IC5.pin14
  N15: BeagleBone1.connectorp8-42, IC3.pin13, IC4.pin13, IC5.pin13
  N16: BeagleBone1.connectorp8-43, IC3.pin16, IC4.pin16, IC5.pin16
  N17: BeagleBone1.connectorp8-44, IC3.pin15, IC4.pin15, IC5.pin15
  N18: BeagleBone1.connectorp8-45, IC3.pin18, IC4.pin18, IC5.pin18
  N19: BeagleBone1.connectorp8-46, IC3.pin17, IC4.pin17, IC5.pin17
  N20: BeagleBone1.connectorp9-3, IC1.pin4, IC1.pin6, IC1.pin8, IC1.pin36, IC2.pin1, IC2.pin20, IC3.pin1, IC3.pin20, IC4.pin1, IC4.pin20, IC5.pin1, IC5.pin20, R1.Pin_0, R2.Pin_0, R3.Pin_0, R4.Pin_0, R5.Pin_0, R6.Pin_1, R7.Pin_1, R8.Pin_1
  N21: BeagleBone1.connectorp9-28, IC5.pin19, R2.Pin_1
  N22: BeagleBone1.connectorp9-29, IC4.pin19, R3.Pin_1
  N23: BeagleBone1.connectorp9-30, IC2.pin19, R1.Pin_1
  N24: BeagleBone1.connectorp9-31, IC3.pin19, R4.Pin_1
  N25: BeagleBone1.connectorp9-43, IC1.pin21, IC2.pin10, IC3.pin10, IC4.pin10, IC5.pin10
  N26: IC1.pin2, R6.Pin_0
  N27: IC1.pin3, R7.Pin_0
  N28: IC1.pin5, R8.Pin_0
  N29: IC1.pin9, IC3.pin2
  N30: IC1.pin10, IC3.pin3
  N31: IC1.pin11, IC3.pin4
  N32: IC1.pin12, IC3.pin5
  N33: IC1.pin13, IC3.pin6
  N34: IC1.pin14, IC3.pin7
  N35: IC1.pin15, IC3.pin8
  N36: IC1.pin16, IC3.pin9
  N37: IC1.pin17, IC4.pin2
  N38: IC1.pin18, IC4.pin3
  N39: IC1.pin19, IC4.pin4
  N40: IC1.pin20, IC4.pin5
  N41: IC1.pin22, IC4.pin6
  N42: IC1.pin23, IC4.pin7
  N43: IC1.pin24, IC4.pin8
  N44: IC1.pin25, IC4.pin9
  N45: IC1.pin26, IC2.pin11, IC5.pin9
  N46: IC1.pin27, IC2.pin12, IC5.pin8
  N47: IC1.pin28, IC2.pin13, IC5.pin7
  N48: IC1.pin29, IC2.pin14, IC5.pin6
  N49: IC1.pin30, IC2.pin15, IC5.pin5
  N50: IC1.pin31, IC2.pin16, IC5.pin4
  N51: IC1.pin32, IC2.pin17, IC5.pin3
  N52: IC1.pin33, IC2.pin18, IC5.pin2
